# Fritzing sketch light (saved by Fritzing 0.9.3b)

parts:
  X1 = USB Connectors [package=usb-mb-h]
  S1 = Toggle Switch [package=THT]
  S2 = Toggle Switch [package=THT]
  DFPlayer_Mini1 = DFPlayer MINI [package="DIP (Dual Inline) [THT]"]
  SP1 = SPEAKER [package=pcb_mount_speaker]
  Part1 = Arduino Uno (Rev3) - ICSP
  R5 = Resistor [tolerance=±5% resistance=10k package=THT]
  R6 = Resistor [tolerance=±5% resistance=10k package=THT]
  R7 = PHOTOCELL [package=photocell-kit]
  R8 = Resistor [tolerance=±5% resistance=10k package=THT]

nets:
  N1: X1.D+, S1.L1
  N2: X1.D-, S2.L2
  N3: X1.GND, DFPlayer_Mini1.GND#9
  N4: S1.COM, DFPlayer_Mini1.USB_+
  N5: S2.COM, DFPlayer_Mini1.USB_-
  N6: DFPlayer_Mini1.VCC, R7.P$2
  N7: DFPlayer_Mini1.RX, R6.Pin_0
  N8: DFPlayer_Mini1.TX, R5.Pin_1
  N9: DFPlayer_Mini1.SPK1, SP1.+
  N10: DFPlayer_Mini1.GND#6, Part1.GND, R8.Pin_0
  N11: DFPlayer_Mini1.SPK2, SP1.-
  N12: Part1.D0/RX, R5.Pin_0
  N13: Part1.D1/TX, R6.Pin_1

custom parts:
  DFPlayer MINI: MP3 module by DFRobot.com for playing Music from an SD-Card. Supports WAV and MP3 files.
